# Fritzing sketch PhysicalSketch (saved by Fritzing 0.9.2b)
perfboards: 1

parts:
  Composant2 = Arduino Nano (Rev3.0)
  Rx1 = mystery part, 4 pins [chip_label=Sensor]
  Tx2 = mystery part, 3 pins [chip_label=Tilt]
  R1 = Resistor [tolerance=±5% resistance=220 package=THT]
  S1 = Toggle Switch [package=THT]
  VCC1 = 4 x AAA Battery Mount
  U1 = LCD-16X2 [package=lcd-16x2]
  Tx1 = mystery part, 3 pins [chip_label=Emitter]  # not connected
  LED2 = LED - 3mm [color="Blue (505nm)" package="3 mm [THT]"]  # not connected

nets:
  N1: Composant2.GND, S1.L1
  N2: Composant2.D2, Rx1.pin3
  N3: Composant2.D4, U1.DB7
  N4: Composant2.D5, U1.DB6
  N5: Composant2.D6, U1.DB5
  N6: Composant2.D7, U1.DB4
  N7: Composant2.D8, U1.E, U1.DB0
  N8: Composant2.D9, U1.RS
  N9: Composant2.D11/MOSI, R1.Pin_0
  N10: Composant2.VIN, VCC1.+
  5V: Composant2.5V, U1.VDD
  N11: Composant2.3V3, U1.A
  N12: Composant2.D13/SCK, Tx2.pin3
  N13: S1.L2, VCC1.-
